# Fritzing sketch DualSevenSegmentDisplays (saved by Fritzing 0.8.7b)
breadboards: 1

parts:
  Part1 = Arduino Uno (Rev3)
  U1 = 74HC595 [package="DIP16 [THT]"]
  R1 = Resistor [tolerance=±5% resistance=220 package=THT]
  R2 = Resistor [tolerance=±5% resistance=220 package=THT]
  R3 = Resistor [tolerance=±5% resistance=220 package=THT]
  R4 = Resistor [tolerance=±5% resistance=220 package=THT]
  R5 = Resistor [tolerance=±5% resistance=220 package=THT]
  R6 = Resistor [tolerance=±5% resistance=220 package=THT]
  R7 = Resistor [tolerance=±5% resistance=220 package=THT]
  U2 = 74HC595 [package="DIP16 [THT]"]
  R8 = Resistor [tolerance=±5% resistance=220 package=THT]
  R9 = Resistor [tolerance=±5% resistance=220 package=THT]
  R10 = Resistor [tolerance=±5% resistance=220 package=THT]
  R11 = Resistor [tolerance=±5% resistance=220 package=THT]
  R12 = Resistor [tolerance=±5% resistance=220 package=THT]
  R13 = Resistor [tolerance=±5% resistance=220 package=THT]
  R14 = Resistor [tolerance=±5% resistance=220 package=THT]
  DI2 = 7-Segment LED Display [package=THT]
  DI3 = 7-Segment LED Display [package=THT]

nets:
  N1: Part1.A0, U1.DS
  N2: Part1.A1, U1.ST_CP
  N3: Part1.A2, U1.SH_CP, U2.SH_CP
  N4: Part1.A3, U2.DS
  N5: Part1.A4/SDA, U2.ST_CP
  VCC: Part1.5V, U1.MR, U1.VCC, U2.MR, U2.VCC
  GND: Part1.GND, U1.GND, U1.OE, U2.GND, U2.OE, DI2.commAnode#2, DI3.commAnode#2
  N6: U1.Q1, R3.Pin_1
  N7: U1.Q2, R4.Pin_1
  N8: U1.Q3, R7.Pin_1
  N9: U1.Q4, R5.Pin_0
  N10: U1.Q5, R6.Pin_0
  N11: U1.Q6, R1.Pin_0
  N12: U1.Q7, R2.Pin_0
  N13: R1.Pin_1, DI2.cathodeF
  N14: R2.Pin_1, DI2.cathodeG
  N15: R3.Pin_0, DI2.cathodeA
  N16: R4.Pin_0, DI2.cathodeB
  N17: R5.Pin_1, DI2.cathodeD
  N18: R6.Pin_1, DI2.cathodeE
  N19: R7.Pin_0, DI2.cathodeC
  N20: U2.Q1, R14.Pin_1
  N21: U2.Q2, R11.Pin_1
  N22: U2.Q3, R8.Pin_1
  N23: U2.Q4, R10.Pin_0
  N24: U2.Q5, R9.Pin_0
  N25: U2.Q6, R13.Pin_0
  N26: U2.Q7, R12.Pin_0
  N27: R8.Pin_0, DI3.cathodeC
  N28: R9.Pin_1, DI3.cathodeE
  N29: R10.Pin_1, DI3.cathodeD
  N30: R11.Pin_0, DI3.cathodeB
  N31: R12.Pin_1, DI3.cathodeG
  N32: R13.Pin_1, DI3.cathodeF
  N33: R14.Pin_0, DI3.cathodeA
